// Logisim project chh182_lab7.circ as structural Verilog: 2 circuits, main circuit main
module main (
);

  wire button_1_out, clk, clock_1_out, done, not_1_out, not_2_out;
  wire [7:0] Multiplier_q, shifter_2_out;
  wire [15:0] adder_1_out, Multiplicand_q, Product_q, shifter_1_out;

  Clock clock_1 (.out(clock_1_out));
  Button button_1 (.out(button_1_out));
  Shifter #(.width(16)) shifter_1 (.in(Multiplicand_q), .\dist (4'b0001), .out(shifter_1_out));
  not not_1 (not_1_out, done);
  Shifter #(.shift("lr")) shifter_2 (.in(Multiplier_q), .\dist (3'b001), .out(shifter_2_out));
  not not_2 (not_2_out, done);
  or or_1 (clk, clock_1_out, button_1_out);
  LED u_Done (.in(done));
  // Probe on Multiplicand_q
  Register #(.width(16)) Multiplicand (.D(shifter_1_out), .en(not_1_out), .Q(Multiplicand_q), .clk(clk));  // open: clr
  Register Multiplier (.D(shifter_2_out), .en(not_2_out), .Q(Multiplier_q), .clk(clk));  // open: clr
  // Probe on Multiplier_q
  // Probe on Product_q
  Adder #(.width(16)) adder_1 (.a(Product_q), .b(Multiplicand_q), .out(adder_1_out));  // open: cin, cout
  Comparator comparator_1 (.a({8{1'b0}}), .b(Multiplier_q), .eq(done));  // open: gt, lt
  Register #(.width(16)) Product (.D(adder_1_out), .en(Multiplier_q[0]), .Q(Product_q), .clk(clk));  // open: clr
endmodule

module Division (
);

  wire and_1_out, button_1_out, clk, clock_1_out, done, larger, not_1_out, not_3_out, not_4_out, smaller;
  wire [7:0] adder_1_out, adder_2_out, adder_3_out, loop_step_q, Quotient_q, register_1_q, register_2_q,
       shifter_2_out;
  wire [15:0] Divisor_q, Remainder_q, shifter_1_out, subtractor_1_out;

  Clock clock_1 (.out(clock_1_out));
  Button button_1 (.out(button_1_out));
  not not_1 (not_1_out, done);
  or or_1 (clk, clock_1_out, button_1_out);
  LED u_Done (.in(done));
  // Probe on Divisor_q
  Register #(.width(16)) Divisor (.D(shifter_1_out), .en(not_1_out), .Q(Divisor_q), .clk(clk));  // open: clr
  Shifter #(.width(16), .shift("lr")) shifter_1 (.in(Divisor_q), .\dist (4'b0001), .out(shifter_1_out));
  Shifter shifter_2 (.in(Quotient_q), .\dist (3'b001), .out(shifter_2_out));
  // Probe on Quotient_q
  Adder adder_1 (.a(shifter_2_out), .b(register_1_q), .out(adder_1_out));  // open: cin, cout
  Register register_1 (.D({8{1'b0}}), .en(larger), .Q(register_1_q), .clk(clk));  // open: clr
  Register register_2 (.D(8'h1), .en(smaller), .Q(register_2_q), .clk(clk));  // open: clr
  // Probe on Remainder_q
  Subtractor #(.width(16)) subtractor_1 (.a(Remainder_q), .b(Divisor_q), .out(subtractor_1_out));  // open: bin, bout
  and and_1 (and_1_out, smaller, done);
  // NOT_Gate not_2 is placed but not wired
  Adder adder_2 (.a(loop_step_q), .b(8'h1), .out(adder_2_out));  // open: cin, cout
  // NOT_Gate not_3 has open pins: in=open, out=not_3_out
  Adder adder_3 (.a(adder_1_out), .b(register_2_q), .out(adder_3_out));  // open: cin, cout
  Register #(.width(16)) Remainder (.D(subtractor_1_out), .en(and_1_out), .Q(Remainder_q), .clk(clk));  // open: clr
  Register loop_step (.D(adder_2_out), .en(not_3_out), .Q(loop_step_q), .clk(clk));  // open: clr
  Comparator comparator_1 (.a(8'h8), .b(loop_step_q), .eq(done));  // open: gt, lt
  // NOT_Gate not_4 has open pins: in=open, out=not_4_out
  Register Quotient (.D(adder_3_out), .en(not_4_out), .Q(Quotient_q), .clk(clk));  // open: clr
  Comparator #(.width(16)) comparator_2 (.a(Divisor_q), .b(Remainder_q), .gt(larger), .lt(smaller));  // open: eq
endmodule
